# Fritzing sketch Diagram (saved by Fritzing 1.0.3b)
circuit board: 8cm x 12cm

parts:
  R19 = Resistor [tolerance=±5% resistance=22k package="0805 [SMD]"]
  R12 = Resistor [tolerance=±5% resistance=22k package="0805 [SMD]"]
  J7 = female pin header, 2 pins [form="♀ (female)"]
  MUX1 = IC, DIP package, 16 pins [chip_label=CDx4HC251]
  R16 = Resistor [tolerance=±5% resistance=22k package="0805 [SMD]"]
  R23 = Resistor [tolerance=±5% resistance=22k package="0805 [SMD]"]
  J5 = female pin header, 2 pins [form="♀ (female)"]
  R30 = Resistor [tolerance=±5% resistance=22k package="0805 [SMD]"]
  R32 = Resistor [tolerance=±5% resistance=22k package="0805 [SMD]"]
  R11 = Resistor [tolerance=±5% resistance=22k package="0805 [SMD]"]
  J6 = female pin header, 2 pins [form="♀ (female)"]
  R8 = Resistor [tolerance=±5% resistance=22k package="0805 [SMD]"]
  MUX4 = IC, DIP package, 16 pins [chip_label=CDx4HC251]
  R15 = Resistor [tolerance=±5% resistance=22k package="0805 [SMD]"]
  R27 = Resistor [tolerance=±5% resistance=22k package="0805 [SMD]"]
  J9 = female pin header, 2 pins [form="♀ (female)"]
  J16 = female pin header, 2 pins [form="♀ (female)"]
  J14 = female pin header, 2 pins [form="♀ (female)"]
  R7 = Resistor [tolerance=±5% resistance=22k package="0805 [SMD]"]
  R24 = Resistor [tolerance=±5% resistance=22k package="0805 [SMD]"]
  R29 = Resistor [tolerance=±5% resistance=22k package="0805 [SMD]"]
  J24 = female pin header, 2 pins [form="♀ (female)"]
  R31 = Resistor [tolerance=±5% resistance=22k package="0805 [SMD]"]
  R21 = Resistor [tolerance=±5% resistance=22k package="0805 [SMD]"]
  R2 = Resistor [tolerance=±5% resistance=22k package="0805 [SMD]"]
  J21 = female pin header, 2 pins [form="♀ (female)"]
  J22 = female pin header, 2 pins [form="♀ (female)"]
  R20 = Resistor [tolerance=±5% resistance=22k package="0805 [SMD]"]
  Mod1 = Raspberry Pi Pico W
  R1 = Resistor [tolerance=±5% resistance=22k package="0805 [SMD]"]
  R14 = Resistor [tolerance=±5% resistance=22k package="0805 [SMD]"]
  J18 = female pin header, 2 pins [form="♀ (female)"]
  J15 = female pin header, 2 pins [form="♀ (female)"]
  R18 = Resistor [tolerance=±5% resistance=22k package="0805 [SMD]"]
  R5 = Resistor [tolerance=±5% resistance=22k package="0805 [SMD]"]
  R10 = Resistor [tolerance=±5% resistance=22k package="0805 [SMD]"]
  J12 = female pin header, 2 pins [form="♀ (female)"]
  R13 = Resistor [tolerance=±5% resistance=22k package="0805 [SMD]"]
  R3 = Resistor [tolerance=±5% resistance=22k package="0805 [SMD]"]
  MUX2 = IC, DIP package, 16 pins [chip_label=CDx4HC251]
  J13 = female pin header, 2 pins [form="♀ (female)"]
  R6 = Resistor [tolerance=±5% resistance=22k package="0805 [SMD]"]
  R25 = Resistor [tolerance=±5% resistance=22k package="0805 [SMD]"]
  J17 = female pin header, 2 pins [form="♀ (female)"]
  R28 = Resistor [tolerance=±5% resistance=22k package="0805 [SMD]"]
  J10 = female pin header, 2 pins [form="♀ (female)"]
  MUX3 = IC, DIP package, 16 pins [chip_label=CDx4HC251]
  J2 = female pin header, 2 pins [form="♀ (female)"]
  R26 = Resistor [tolerance=±5% resistance=22k package="0805 [SMD]"]
  J23 = female pin header, 2 pins [form="♀ (female)"]
  J19 = female pin header, 2 pins [form="♀ (female)"]
  J11 = female pin header, 2 pins [form="♀ (female)"]
  J1 = female pin header, 2 pins [form="♀ (female)"]
  J3 = female pin header, 2 pins [form="♀ (female)"]
  R4 = Resistor [tolerance=±5% resistance=22k package="0805 [SMD]"]
  J4 = female pin header, 2 pins [form="♀ (female)"]
  J20 = female pin header, 2 pins [form="♀ (female)"]
  R9 = Resistor [tolerance=±5% resistance=22k package="0805 [SMD]"]
  R22 = Resistor [tolerance=±5% resistance=22k package="0805 [SMD]"]
  J8 = female pin header, 2 pins [form="♀ (female)"]
  R17 = Resistor [tolerance=±5% resistance=22k package="0805 [SMD]"]
  B1_IN = female pin header, 2 pins [form="♀ (female)"]
  B1_Out = female pin header, 2 pins [form="♀ (female)"]
  J25 = female pin header, 2 pins [form="♀ (female)"]

nets:
  N1: R19.Pin_0, J12.pin1, MUX3.pin14
  GND: R19.Pin_1, R12.Pin_1, MUX1.pin7, MUX1.pin8, R16.Pin_1, R23.Pin_1, R30.Pin_1, R32.Pin_1, R11.Pin_1, R8.Pin_1, MUX4.pin7, MUX4.pin8, R15.Pin_1, R27.Pin_1, R7.Pin_1, R24.Pin_1, R29.Pin_1, J24.pin1, R31.Pin_1, R21.Pin_1, R2.Pin_1, J21.pin1, J22.pin1, R20.Pin_1, Mod1.pin_18, Mod1.pin_23, Mod1.pin_28, Mod1.pin_38, Mod1.pin_42, R1.Pin_1, R14.Pin_1, J18.pin1, R18.Pin_1, R5.Pin_1, R10.Pin_1, R13.Pin_1, R3.Pin_1, MUX2.pin7, MUX2.pin8, R6.Pin_1, R25.Pin_1, J17.pin1, R28.Pin_1, MUX3.pin7, MUX3.pin8, R26.Pin_1, J23.pin1, J19.pin1, R4.Pin_1, J20.pin1, R9.Pin_1, R22.Pin_1, R17.Pin_1, J25.pin2
  N2: R12.Pin_0, J6.pin1, MUX2.pin1
  N3: J7.pin1, R10.Pin_0, MUX2.pin13
  N4: J7.pin2, R16.Pin_0, MUX2.pin12
  N5: MUX1.pin1, R1.Pin_0, J2.pin1
  N6: MUX1.pin2, R2.Pin_0, J2.pin2
  N7: MUX1.pin3, J1.pin2, R4.Pin_0
  N8: MUX1.pin4, R3.Pin_0, J1.pin1
  Y0: MUX1.pin5, Mod1.pin_15
  S2: MUX1.pin9, MUX4.pin9, Mod1.pin_24, MUX2.pin9, MUX3.pin9
  S1: MUX1.pin10, MUX4.pin10, Mod1.pin_22, MUX2.pin10, MUX3.pin10
  S0: MUX1.pin11, MUX4.pin11, Mod1.pin_21, MUX2.pin11, MUX3.pin11
  N9: MUX1.pin12, R6.Pin_0, J3.pin2
  N10: MUX1.pin13, R5.Pin_0, J3.pin1
  N11: MUX1.pin14, R7.Pin_0, J4.pin1
  N12: MUX1.pin15, R8.Pin_0, J4.pin2
  3.3V: MUX1.pin16, MUX4.pin16, J24.pin2, J21.pin2, J22.pin2, Mod1.pin_36, J18.pin2, MUX2.pin16, J17.pin2, MUX3.pin16, J23.pin2, J19.pin2, J20.pin2, B1_IN.pin1, B1_IN.pin2
  N13: R23.Pin_0, J9.pin2, MUX3.pin3
  N14: J5.pin1, R14.Pin_0, MUX2.pin4
  N15: J5.pin2, R15.Pin_0, MUX2.pin3
  N16: R30.Pin_0, MUX4.pin4, J13.pin1
  N17: R32.Pin_0, MUX4.pin12, J15.pin2
  N18: R11.Pin_0, MUX2.pin14, J8.pin1
  N19: J6.pin2, MUX2.pin2, R9.Pin_0
  N20: MUX4.pin1, J14.pin1, R28.Pin_0
  N21: MUX4.pin2, J14.pin2, R25.Pin_0
  N22: MUX4.pin3, R31.Pin_0, J13.pin2
  Y3: MUX4.pin5, Mod1.pin_11
  N23: MUX4.pin13, J15.pin1, R26.Pin_0
  N24: MUX4.pin14, R27.Pin_0, J16.pin1
  N25: MUX4.pin15, J16.pin2, R29.Pin_0
  N26: J9.pin1, MUX3.pin4, R22.Pin_0
  N27: R24.Pin_0, MUX3.pin12, J11.pin2
  N28: R21.Pin_0, J12.pin2, MUX3.pin15
  N29: R20.Pin_0, J10.pin1, MUX3.pin1
  Y2: Mod1.pin_12, MUX3.pin5
  Y1: Mod1.pin_14, MUX2.pin5
  BUT: Mod1.pin_20, B1_Out.pin1, B1_Out.pin2
  N30: Mod1.pin_39, J25.pin1
  N31: R18.Pin_0, MUX3.pin13, J11.pin1
  N32: R13.Pin_0, MUX2.pin15, J8.pin2
  N33: J10.pin2, MUX3.pin2, R17.Pin_0

notes:
  Part IV Project 26
  Matthew Taylor, Victoria Jones
  Department of Electrical, Computer, and Software Engineering
  2024
  University of Auckland - Faculty of Engineering

custom parts:
  Raspberry Pi Pico W: Raspberry Pi Pico W. Based around the RP2040 microcontroller the Pico W is a low cost microcontroller device bringing Raspberry Pi quality, cost, and easy of use to the microcontroller space. The areas marked KEEPOUT in pcb silkscreen should not have traces running through them to avoid shorts on a soldered in module!
