# Fritzing sketch SR NAND (saved by Fritzing 1.0.3b)
breadboards: 1

parts:
  NAND = 74HC00; 74HCT00 [chip_label=74HC00 package="DIP (Dual Inline) [THT]"]
  Pico_W = Raspberry Pi Pico W
  LED1 = smd LED [color="Red (633nm)" package="0805 [SMD]"]
  LED2 = smd LED [color="Red (633nm)" package="0805 [SMD]"]

nets:
  GND: NAND.GND, Pico_W.pin_8, Pico_W.pin_33, LED1.cathode, LED2.cathode
  N1: NAND.3Y, NAND.4A, LED1.anode
  reset: NAND.3A, Pico_W.pin_2
  N2: NAND.3B, NAND.4Y, LED2.anode
  set: NAND.4B, Pico_W.pin_1
  3.3V: NAND.VCC, Pico_W.pin_36

custom parts:
  74HC00; 74HCT00: Quad 2-input NAND gate
  Raspberry Pi Pico W: Raspberry Pi Pico W. Based around the RP2040 microcontroller the Pico W is a low cost microcontroller device bringing Raspberry Pi quality, cost, and easy of use to the microcontroller space. The areas marked KEEPOUT in pcb silkscreen should not have traces running through them to avoid shorts on a soldered in module!
