# Fritzing sketch Untitled Sketch (saved by Fritzing 1.0.3b)
breadboards: 1

parts:
  Pico_W = Raspberry Pi Pico W
  MUX1 = DIP - 28 pins [chip_label=MAX306CPI package="DIP (Dual Inline) [THT]"]
  V1 = DC Power [voltage=5V internal_resistance=0.1Ω]  # not connected

nets:
  N1: Pico_W.pin_1, MUX1.COM
  N2: Pico_W.pin_24, MUX1.A0
  N3: Pico_W.pin_25, MUX1.A1
  N4: Pico_W.pin_26, MUX1.A2
  N5: Pico_W.pin_27, MUX1.A3
  GND: MUX1.V-

custom parts:
  Raspberry Pi Pico W: Raspberry Pi Pico W. Based around the RP2040 microcontroller the Pico W is a low cost microcontroller device bringing Raspberry Pi quality, cost, and easy of use to the microcontroller space. The areas marked KEEPOUT in pcb silkscreen should not have traces running through them to avoid shorts on a soldered in module!
  DIP - 28 pins: A DIP stand-in part for whatever IC you want. With 28 pins on a 300mil dual inline package (DIP) footprint.
